# Fritzing sketch calculator (saved by Fritzing 1.0.1rc)
circuit board: 11.5cm x 11.5cm
breadboards: 2

parts:
  RPi_Pico = Raspberry Pi Pico
  SW1 = DIP SWITCH [package=dipswitch-02]
  SW2 = DIP SWITCH [package=dipswitch-02]
  Nano = Arduino Nano (Rev3.0) (ICSP)
  TFT = TFT 1.8 inch 160x128 w SD
  S1 = Pushbutton [package="[THT]"]
  S2 = Pushbutton [package="[THT]"]
  S3 = Pushbutton [package="[THT]"]
  S4 = Pushbutton [package="[THT]"]
  S5 = Pushbutton [package="[THT]"]
  S6 = Pushbutton [package="[THT]"]
  S7 = Pushbutton [package="[THT]"]
  S8 = Pushbutton [package="[THT]"]
  S9 = Pushbutton [package="[THT]"]
  S10 = Pushbutton [package="[THT]"]
  S11 = Pushbutton [package="[THT]"]
  S12 = Pushbutton [package="[THT]"]
  S13 = Pushbutton [package="[THT]"]
  S14 = Pushbutton [package="[THT]"]
  S15 = Pushbutton [package="[THT]"]
  S16 = Pushbutton [package="[THT]"]
  S17 = Pushbutton [package="[THT]"]
  S18 = Pushbutton [package="[THT]"]
  S19 = Pushbutton [package="[THT]"]
  S20 = Pushbutton [package="[THT]"]
  S21 = Pushbutton [package="[THT]"]
  S22 = Pushbutton [package="[THT]"]
  S23 = Pushbutton [package="[THT]"]
  S24 = Pushbutton [package="[THT]"]
  S25 = Pushbutton [package="[THT]"]
  S26 = Pushbutton [package="[THT]"]
  S27 = Pushbutton [package="[THT]"]
  S28 = Pushbutton [package="[THT]"]
  S29 = Pushbutton [package="[THT]"]
  S30 = Pushbutton [package="[THT]"]
  S31 = Pushbutton [package="[THT]"]
  S32 = Pushbutton [package="[THT]"]
  S33 = Pushbutton [package="[THT]"]
  S34 = Pushbutton [package="[THT]"]
  S35 = Pushbutton [package="[THT]"]
  S36 = Pushbutton [package="[THT]"]
  JACK = 3.5mm Audio Jack [package=audio-jack-3.5mm-smd]
  Pad1 = Pad [width=1.8583494138876684 height=2.784559596650767 connect=center]
  Pad2 = Pad [width=1.9612438690149454 height=2.8852090697271295 connect=center]
  R7 = Resistor [tolerance=±1% power=0.25 resistance=330 package=THT]
  R8 = Resistor [tolerance=±1% power=0.25W resistance=330 package=THT]
  R9 = Resistor [tolerance=±5% power=0.25 resistance=4.7k package=THT]
  R10 = Resistor [tolerance=±5% power=0.25 resistance=4.7k package=THT]
  3V3 = Pad [width=1.6260647170979612 height=2.704457124362391 connect=center]
  J1 = Power Jack [package=power_jack_slot]

nets:
  GND: RPi_Pico.pin_3, RPi_Pico.pin_8, RPi_Pico.pin_13, RPi_Pico.pin_18, RPi_Pico.pin_23, RPi_Pico.pin_28, RPi_Pico.pin_33, RPi_Pico.pin_38, RPi_Pico.pin_42, SW1.1, SW1.2, SW2.1, SW2.2, Nano.GND, TFT.pin2, JACK.SLEEVE, Pad2.pad, J1.GNDBREAK, J1.GND
  N1: RPi_Pico.pin_5, JACK.RIGHT
  N2: RPi_Pico.pin_6, JACK.LEFT
  N3: RPi_Pico.pin_11, TFT.pin_11
  N4: RPi_Pico.pin_12, TFT.pin_9
  N5: RPi_Pico.pin_14, TFT.pin_12
  N6: RPi_Pico.pin_15, TFT.pin_10
  N7: RPi_Pico.pin_16, SW2.4
  N8: RPi_Pico.pin_17, SW2.3
  N9: RPi_Pico.pin_19, SW1.4
  N10: RPi_Pico.pin_20, SW1.3
  N11: RPi_Pico.pin_22, TFT.pin3
  N12: RPi_Pico.pin_24, TFT.pin_7
  N13: RPi_Pico.pin_25, TFT.pin_6
  N14: RPi_Pico.pin_26, TFT.pin4
  N15: RPi_Pico.pin_27, TFT.pin_5
  N16: RPi_Pico.pin_29, TFT.pin_8
  N17: RPi_Pico.pin_31, R8.Pin_0, R9.Pin_0
  N18: RPi_Pico.pin_32, R7.Pin_0, R10.Pin_0
  N19: RPi_Pico.pin_36, TFT.pin_1, R9.Pin_1, R10.Pin_1, 3V3.pad
  N20: RPi_Pico.pin_39, Nano.5V, Pad1.pad
  N21: Nano.D2, S1.Pin_3, S1.Pin_4, S2.Pin_3, S2.Pin_4, S3.Pin_3, S3.Pin_4, S4.Pin_3, S4.Pin_4, S5.Pin_3, S5.Pin_4, S6.Pin_3, S6.Pin_4
  N22: Nano.D3, S7.Pin_3, S7.Pin_4, S8.Pin_3, S8.Pin_4, S9.Pin_3, S9.Pin_4, S10.Pin_3, S10.Pin_4, S11.Pin_3, S11.Pin_4, S12.Pin_3, S12.Pin_4
  N23: Nano.D4, S13.Pin_3, S13.Pin_4, S14.Pin_3, S14.Pin_4, S15.Pin_3, S15.Pin_4, S16.Pin_3, S16.Pin_4, S17.Pin_3, S17.Pin_4, S18.Pin_3, S18.Pin_4
  N24: Nano.D5, S19.Pin_3, S19.Pin_4, S20.Pin_3, S20.Pin_4, S21.Pin_3, S21.Pin_4, S22.Pin_3, S22.Pin_4, S23.Pin_3, S23.Pin_4, S24.Pin_3, S24.Pin_4
  N25: Nano.D6, S25.Pin_3, S25.Pin_4, S26.Pin_3, S26.Pin_4, S27.Pin_3, S27.Pin_4, S28.Pin_3, S28.Pin_4, S29.Pin_3, S29.Pin_4, S30.Pin_3, S30.Pin_4
  N26: Nano.D7, S31.Pin_3, S31.Pin_4, S32.Pin_3, S32.Pin_4, S33.Pin_3, S33.Pin_4, S34.Pin_3, S34.Pin_4, S35.Pin_3, S35.Pin_4, S36.Pin_3, S36.Pin_4
  N27: Nano.D8, S1.Pin_2, S7.Pin_1, S7.Pin_2, S13.Pin_1, S13.Pin_2, S19.Pin_1, S19.Pin_2, S25.Pin_1, S25.Pin_2, S31.Pin_1, S31.Pin_2
  N28: Nano.D9, S2.Pin_2, S8.Pin_1, S8.Pin_2, S14.Pin_1, S14.Pin_2, S20.Pin_1, S20.Pin_2, S26.Pin_1, S26.Pin_2, S32.Pin_1, S32.Pin_2
  N29: Nano.D10, S3.Pin_2, S9.Pin_1, S9.Pin_2, S15.Pin_1, S15.Pin_2, S21.Pin_1, S21.Pin_2, S27.Pin_1, S27.Pin_2, S33.Pin_1, S33.Pin_2
  N30: Nano.D11/MOSI, S4.Pin_1, S4.Pin_2, S10.Pin_1, S10.Pin_2, S16.Pin_1, S16.Pin_2, S22.Pin_1, S22.Pin_2, S28.Pin_1, S28.Pin_2, S34.Pin_1, S34.Pin_2
  N31: Nano.D12/MISO, S5.Pin_1, S5.Pin_2, S11.Pin_1, S11.Pin_2, S17.Pin_1, S17.Pin_2, S23.Pin_1, S23.Pin_2, S29.Pin_1, S29.Pin_2, S35.Pin_1, S35.Pin_2
  N32: Nano.VIN, J1.PWR
  N33: Nano.A5, R7.Pin_1
  N34: Nano.A4, R8.Pin_1
  N35: Nano.D13/SCK, S6.Pin_2, S12.Pin_1, S12.Pin_2, S18.Pin_1, S18.Pin_2, S24.Pin_1, S24.Pin_2, S30.Pin_1, S30.Pin_2, S36.Pin_1, S36.Pin_2

notes:
  5V
  GND
  https://github.com/hdkghc/calculator
  SHIFT   ALPHA    CTRL     x      OPTN     ON
  √      ^      ²      (      )     lg
  7       8       9      tan     DEL     AC
  4       5      6      cos     ×       ÷
  1       2       3     sin      +      -
  0       .      EE      FMT     Ans     EXE
  SD
  Copyright (c) 2026 hdkghc
  4k7
  330

custom parts:
  Raspberry Pi Pico: Raspberry Pi Pico. Based around the RP2040 microcontroller the Pico is a low cost microcontroller device bringing Raspberry Pi quality, cost, and easy of use to the microcontroller space. Jan 2021, Split part in to two versions: tht (this one) and SMD. This one will drill holes for a .1 in header in pcb to allow plugging in the module as well as providing pads to solder the module to the top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
  TFT 1.8 inch 160x128 w SD: This is a generic 1.8 tft spi lcd display available on ebay and others. The 1.8" display has 128x160 color pixels.
